# Fritzing sketch Road (saved by Fritzing 0.9.3b)

parts:
  U1 = NodeMCU V3.0
  M1 = fc-51 [package=THT]
  M2 = fc-51 [package=THT]
  J1 = Basic Servo
  Grove1 = Grove OLED 128x96
  Grove2 = Grove OLED 128x96

nets:
  N1: U1.3V3, M1.pin3, M2.pin3
  N2: U1.D5, J1.pulse
  N3: U1.D6, M2.pin1
  N4: U1.D7, M1.pin1
  VIN: U1.Vin, J1.vcc
  N5: U1.GND#16, U1.GND#33, J1.gnd
  N6: M1.pin2, M2.pin2
  GND: Grove1.GND, Grove2.GND
  VCC: Grove1.VCC, Grove2.VCC
  N7: Grove1.SDA, Grove2.SDA
  N8: Grove1.SCL, Grove2.SCL

custom parts:
  NodeMCU V3.0: ESP8266 based NodeMCU
