# Fritzing sketch car (saved by Fritzing 0.9.3b)

parts:
  U1 = NodeMCU V3.0
  A1 = Motor driver tzt DRV8833
  M1 = DC Motor
  M2 = DC Motor
  HC-SR04_Sensor_1 = HC-SR04 Ultrasonic Distance Sensor
  VCC1 = Battery
  M3 = RioRand LM2596

nets:
  N1: U1.D0, HC-SR04_Sensor_1.ECHO
  N2: U1.D1, A1.Pin_7
  N3: U1.D2, A1.Pin_8
  N4: U1.GND, M3.Pin_4
  N5: U1.D5, A1.Pin_11
  N6: U1.D6, A1.Pin_12
  N7: U1.D7, HC-SR04_Sensor_1.TRIG
  N8: U1.Vin, M3.Pin_3
  N9: A1.Pin_2, M2.pin_2
  N10: A1.Pin_3, M2.pin_1
  N11: A1.Pin_4, M1.pin_1
  N12: A1.Pin_5, M1.pin_2
  N13: VCC1.-, M3.Pin_2
  N14: VCC1.+, M3.Pin_1

notes:
  Car 1  &  Car 2

custom parts:
  NodeMCU V3.0: ESP8266 based NodeMCU
  Motor driver tzt DRV8833: TZT DRV8833 DC3V-10V 1.5A 2 Channel DC Motor Drive Module.
